# Fritzing sketch CNC 3 (saved by Fritzing 0.9.3b)
breadboards: 1

parts:
  Componente1 = Arduino Mega ADK (Rev3)
  M2 = Stepper Motor - Bipolar
  S1 = Pushbutton [package="[THT]"]
  S3 = H-Bridge with L298N
  M3 = Stepper Motor - Bipolar
  S4 = H-Bridge with L298N
  J2 = Basic Servo
  Componente2 = Thumb Joystick
  Power_plug1 = Power plug
  R1 = Resistor [tolerance=±5% resistance=220 package=THT]

nets:
  N1: Componente1.A0, Componente2.HORZ
  N2: Componente1.A1, Componente2.VERT
  N3: Componente1.D12_PWM, S3.IN1
  N4: Componente1.D11_PWM, S3.IN2
  N5: Componente1.D10_PWM, S3.IN3
  N6: Componente1.D9_PWM, S3.IN4
  GND: Componente1.GND, S3.GND, S4.GND, J2.gnd, Componente2.GND, Power_plug1.GND, R1.Pin_1
  N7: Componente1.D2_PWM, S4.IN1
  N8: Componente1.D3_PWM, S4.IN2
  N9: Componente1.D5_PWM, S4.IN4
  N10: Componente1.D47, J2.pulse
  VCC: Componente1.D49, S1.Pin_1, S1.Pin_2, S1.Pin_3, S1.Pin_4, S3.5V, S4.5V, J2.vcc, Componente2.VCC, Power_plug1.VCC, R1.Pin_0
  N11: M2.A, S3.M1-02
  N12: M2.C, S3.M1-01
  N13: M2.B, S3.M2-02
  N14: M2.D, S3.M2-01
  N15: S3.ENA, S3.ENA-5V
  N16: S3.ENB, S3.ENB-5V
  N17: M3.A, S4.M1-02
  N18: M3.C, S4.M1-01
  N19: M3.B, S4.M2-02
  N20: M3.D, S4.M2-01
  N21: S4.ENA, S4.ENA-5V
  N22: S4.ENB, S4.ENB-5V

custom parts:
  H-Bridge with L298N: h-bridge

// code stored in the sketch: CNC.ino
//Incluir Biblioteca Stepper --> Controle do motor de passo
//Incluir Bibliotec Servo --> Controle Servo Motor
#include <Stepper.h>
#include <Servo.h>

//Definir os Pinos
const int X_pin = A0; // Pot em X conectado em AO
const int Y_pin = A1; // Pot em Y conectado em A1 
const int botao_pin = 47; //Pino conectado o botao para o Servo --> Pulldown
const int Servo_pin = 49; //Pino que o Servo está conectado


//Passos para dar uma volta
const int stepsPerRevolution = 20; //MOTOR DE CD

// Criar instancias de motor de Passo  e Servo
Stepper Motor_x(stepsPerRevolution, 12, 11, 10, 9); //Motor X 
Stepper Motor_y(stepsPerRevolution, 2, 3, 4, 5); //Motor Y
Servo Motor_caneta; //Motor Caneta

//Quantos passos irá dar 
int passos = 1; //MAX 250

// Variavel para amarzenar a posicao do servo
int counter = 0;


void setup() {
  Serial.begin(9600);
  Motor_caneta.attach(Servo_pin);
  pinMode(botao_pin, INPUT);
  pinMode(X_pin, INPUT);
  pinMode(Y_pin, INPUT);
}

void loop() {
  //Controle moviemnto da caneta
  //Variavel para definir o estado do botao
  int buttonState;  

  //le o estado do botao e grava isso
  buttonState = digitalRead(botao_pin);

  //Se o Botao for pressionado, adiciona isso no counter e da um delay --> "D"ebounce
  if (buttonState == HIGH) // 
  {
    counter++;
    delay(150);
  }
  if(counter == 0){
    Motor_caneta.write (20);}  // Zero Graus
  else if(counter == 1){
    Motor_caneta.write(90);}
  else if(counter == 2){
    Motor_caneta.write (150); }
  else if(counter == 3){  
    Motor_caneta.write (180);}
  //else reset the counter to 0 which resets thr servo to 0 degrees
  else{
   counter = 0;
  }
  //Controle Motor de Passo 
  int val_x = analogRead(X_pin);
  int val_y = analogRead(Y_pin);

  //Motor Parado caso Joystick esteja no meio
  if( (val_x > 450) && (val_x < 523) && (val_y > 450) && (val_y < 523)){
    delay(20);
  }
  else{
    //Mover o motor_x em uma direcao
    while (val_x >= 523){
      // map the speed between 30 and 100 rpm
      int speed_x = map(val_x, 523, 1023, 60, 120);
      // set motor speed
      Motor_x.setSpeed(speed_x);
 
      // move the motor (1 step)
      Motor_x.step(1);
 
      val_x = analogRead(X_pin);
    }
   //Mover o motor_x na outra direcao
    while (val_x <= 450){
      // map the speed between 5 and 500 rpm
      int speed_x = map(val_x, 450, 0, 60, 120);
      // set motor speed
      Motor_x.setSpeed(speed_x);
 
      // move the motor (1 step)
      Motor_x.step(-1);
 
      val_x = analogRead(X_pin);
    }
   }
//////////////
 //Mover o motor_y em uma direcao
    while (val_y >= 523){
      // map the speed between 30 and 100 rpm
      int speed_y = map(val_y, 523, 1023, 60, 120);
      // set motor speed
      Motor_y.setSpeed(speed_y);
 
      // move the motor (1 step)
      Motor_y.step(1);
 
      val_y = analogRead(Y_pin);
    }
   //Mover o motor_y na outra direcao
    while (val_y <= 450){
      // map the speed between 5 and 500 rpm
      int speed_y = map(val_y, 450, 0, 60, 120);
      // set motor speed
      Motor_y.setSpeed(speed_y);
 
      // move the motor (1 step)
      Motor_y.step(-1);
 
      val_y = analogRead(Y_pin);
    }
   }
